// Logisim project 16_BIT_ADD_SUB.circ as structural Verilog: 1 circuit, main circuit main
module main (
  input  B15,
  input  B14,
  input  B13,
  input  B12,
  input  B11,
  input  B10,
  input  B9,
  input  B8,
  input  B7,
  input  B6,
  input  B5,
  input  B4,
  input  B3,
  input  B2,
  input  B1,
  input  B0,
  input  A15,
  input  A14,
  input  A13,
  input  A12,
  input  A11,
  input  A10,
  input  A9,
  input  A8,
  input  A7,
  input  A6,
  input  A5,
  input  A4,
  input  A3,
  input  A2,
  input  A1,
  input  A0,
  input  SUB,
  input  C_IN,
  output Overflow,
  output S15,
  output S14,
  output S13,
  output S12,
  output S11,
  output S10,
  output S9,
  output S8,
  output S7,
  output S6,
  output S5,
  output S4,
  output S3,
  output S2,
  output S1,
  output S0
);

  wire main_2_c_out, main_3_c_out, main_4_c_out, main_5_c_out, main_6_c_out, main_7_c_out, main_8_c_out,
       main_9_c_out, main_10_c_out, main_11_c_out, main_12_c_out, main_13_c_out, main_14_c_out,
       main_15_c_out, main_16_c_out, or_1_out, xor_1_out, xor_2_out, xor_3_out, xor_4_out, xor_5_out,
       xor_6_out, xor_7_out, xor_8_out, xor_9_out, xor_10_out, xor_11_out, xor_12_out, xor_13_out,
       xor_14_out, xor_15_out, xor_16_out;

  xor xor_1 (xor_1_out, SUB, A15);
  _1_bit_full_adder_main main_1 (.A(xor_1_out), .B(B15), .C_in(main_3_c_out), .Sum(S15), .C_out(Overflow));
  xor xor_2 (xor_2_out, SUB, A14);
  xor xor_3 (xor_3_out, SUB, A13);
  _1_bit_full_adder_main main_2 (.A(xor_3_out), .B(B13), .C_in(main_4_c_out), .Sum(S13), .C_out(main_2_c_out));
  _1_bit_full_adder_main main_3 (.A(xor_2_out), .B(B14), .C_in(main_2_c_out), .Sum(S14), .C_out(main_3_c_out));
  xor xor_4 (xor_4_out, SUB, A12);
  xor xor_5 (xor_5_out, SUB, A11);
  _1_bit_full_adder_main main_4 (.A(xor_4_out), .B(B12), .C_in(main_5_c_out), .Sum(S12), .C_out(main_4_c_out));
  _1_bit_full_adder_main main_5 (.A(xor_5_out), .B(B11), .C_in(main_7_c_out), .Sum(S11), .C_out(main_5_c_out));
  xor xor_6 (xor_6_out, SUB, A9);
  xor xor_7 (xor_7_out, SUB, A10);
  _1_bit_full_adder_main main_6 (.A(xor_6_out), .B(B9), .C_in(main_9_c_out), .Sum(S9), .C_out(main_6_c_out));
  _1_bit_full_adder_main main_7 (.A(xor_7_out), .B(B10), .C_in(main_6_c_out), .Sum(S10), .C_out(main_7_c_out));
  xor xor_8 (xor_8_out, SUB, A7);
  xor xor_9 (xor_9_out, SUB, A8);
  _1_bit_full_adder_main main_8 (.A(xor_8_out), .B(B7), .C_in(main_11_c_out), .Sum(S7), .C_out(main_8_c_out));
  _1_bit_full_adder_main main_9 (.A(xor_9_out), .B(B8), .C_in(main_8_c_out), .Sum(S8), .C_out(main_9_c_out));
  xor xor_10 (xor_10_out, SUB, A5);
  xor xor_11 (xor_11_out, SUB, A6);
  _1_bit_full_adder_main main_10 (.A(xor_10_out), .B(B5), .C_in(main_13_c_out), .Sum(S5), .C_out(main_10_c_out));
  _1_bit_full_adder_main main_11 (.A(xor_11_out), .B(B6), .C_in(main_10_c_out), .Sum(S6), .C_out(main_11_c_out));
  xor xor_12 (xor_12_out, SUB, A3);
  xor xor_13 (xor_13_out, SUB, A4);
  _1_bit_full_adder_main main_12 (.A(xor_12_out), .B(B3), .C_in(main_14_c_out), .Sum(S3), .C_out(main_12_c_out));
  _1_bit_full_adder_main main_13 (.A(xor_13_out), .B(B4), .C_in(main_12_c_out), .Sum(S4), .C_out(main_13_c_out));
  xor xor_14 (xor_14_out, SUB, A1);
  xor xor_15 (xor_15_out, SUB, A2);
  _1_bit_full_adder_main main_14 (.A(xor_15_out), .B(B2), .C_in(main_15_c_out), .Sum(S2), .C_out(main_14_c_out));
  _1_bit_full_adder_main main_15 (.A(xor_14_out), .B(B1), .C_in(main_16_c_out), .Sum(S1), .C_out(main_15_c_out));
  xor xor_16 (xor_16_out, SUB, A0);
  or or_1 (or_1_out, SUB, C_IN);
  _1_bit_full_adder_main main_16 (.A(xor_16_out), .B(B0), .C_in(or_1_out), .Sum(S0), .C_out(main_16_c_out));
endmodule
