// Logisim project 16_bit_tristate_buffer.circ as structural Verilog: 1 circuit, main circuit main
module main (
  input  [15:0] In,
  input  S0,
  input  S1,
  input  S2,
  input  S3,
  output [15:0] Out
);

  wire and_1_out;

  assign Out = and_1_out ? In : 16'bz;  // Controlled_Buffer controlled_buffer_1
  and and_1 (and_1_out, S0, S1, S2, S3);
endmodule
