// Logisim project 1_bit_full_adder.circ as structural Verilog: 1 circuit, main circuit main
module main (
  input  A,
  input  B,
  input  C_in,
  output Sum,
  output C_out
);

  wire and_1_out, and_2_out, xor_1_out;

  xor xor_1 (xor_1_out, A, B);
  and and_1 (and_1_out, C_in, xor_1_out);
  and and_2 (and_2_out, B, A);
  xor xor_2 (Sum, xor_1_out, C_in);
  or or_1 (C_out, and_1_out, and_2_out);
endmodule
