// Logisim project 32_bit_D_register.circ as structural Verilog: 1 circuit, main circuit main
module main (
  input  Clk,
  input  OE,
  input  WE,
  input  [31:0] In,
  output [31:0] Out
);

  wire main_1_clk_o;

  Rising_edge_main main_1 (.CLK_i(Clk), .CLK_o(main_1_clk_o));
  D_latch_main main_2 (.D_in(In[30]), .Clk(main_1_clk_o), .OE(OE), .WE(WE), .D_out(Out[30]));
  D_latch_main main_3 (.D_in(In[31]), .Clk(main_1_clk_o), .OE(OE), .WE(WE), .D_out(Out[31]));
  D_latch_main main_4 (.D_in(In[29]), .Clk(main_1_clk_o), .OE(OE), .WE(WE), .D_out(Out[29]));
  D_latch_main main_5 (.D_in(In[28]), .Clk(main_1_clk_o), .OE(OE), .WE(WE), .D_out(Out[28]));
  D_latch_main main_6 (.D_in(In[27]), .Clk(main_1_clk_o), .OE(OE), .WE(WE), .D_out(Out[27]));
  D_latch_main main_7 (.D_in(In[26]), .Clk(main_1_clk_o), .OE(OE), .WE(WE), .D_out(Out[26]));
  D_latch_main main_8 (.D_in(In[25]), .Clk(main_1_clk_o), .OE(OE), .WE(WE), .D_out(Out[25]));
  D_latch_main main_9 (.D_in(In[24]), .Clk(main_1_clk_o), .OE(OE), .WE(WE), .D_out(Out[24]));
  D_latch_main main_10 (.D_in(In[23]), .Clk(main_1_clk_o), .OE(OE), .WE(WE), .D_out(Out[23]));
  D_latch_main main_11 (.D_in(In[22]), .Clk(main_1_clk_o), .OE(OE), .WE(WE), .D_out(Out[22]));
  D_latch_main main_12 (.D_in(In[21]), .Clk(main_1_clk_o), .OE(OE), .WE(WE), .D_out(Out[21]));
  D_latch_main main_13 (.D_in(In[20]), .Clk(main_1_clk_o), .OE(OE), .WE(WE), .D_out(Out[20]));
  D_latch_main main_14 (.D_in(In[19]), .Clk(main_1_clk_o), .OE(OE), .WE(WE), .D_out(Out[19]));
  D_latch_main main_15 (.D_in(In[18]), .Clk(main_1_clk_o), .OE(OE), .WE(WE), .D_out(Out[18]));
  D_latch_main main_16 (.D_in(In[16]), .Clk(main_1_clk_o), .OE(OE), .WE(WE), .D_out(Out[16]));
  D_latch_main main_17 (.D_in(In[17]), .Clk(main_1_clk_o), .OE(OE), .WE(WE), .D_out(Out[17]));
  D_latch_main main_18 (.D_in(In[15]), .Clk(main_1_clk_o), .OE(OE), .WE(WE), .D_out(Out[15]));
  D_latch_main main_19 (.D_in(In[13]), .Clk(main_1_clk_o), .OE(OE), .WE(WE), .D_out(Out[13]));
  D_latch_main main_20 (.D_in(In[14]), .Clk(main_1_clk_o), .OE(OE), .WE(WE), .D_out(Out[14]));
  D_latch_main main_21 (.D_in(In[12]), .Clk(main_1_clk_o), .OE(OE), .WE(WE), .D_out(Out[12]));
  D_latch_main main_22 (.D_in(In[11]), .Clk(main_1_clk_o), .OE(OE), .WE(WE), .D_out(Out[11]));
  D_latch_main main_23 (.D_in(In[10]), .Clk(main_1_clk_o), .OE(OE), .WE(WE), .D_out(Out[10]));
  D_latch_main main_24 (.D_in(In[9]), .Clk(main_1_clk_o), .OE(OE), .WE(WE), .D_out(Out[9]));
  D_latch_main main_25 (.D_in(In[8]), .Clk(main_1_clk_o), .OE(OE), .WE(WE), .D_out(Out[8]));
  D_latch_main main_26 (.D_in(In[7]), .Clk(main_1_clk_o), .OE(OE), .WE(WE), .D_out(Out[7]));
  D_latch_main main_27 (.D_in(In[6]), .Clk(main_1_clk_o), .OE(OE), .WE(WE), .D_out(Out[6]));
  D_latch_main main_28 (.D_in(In[5]), .Clk(main_1_clk_o), .OE(OE), .WE(WE), .D_out(Out[5]));
  D_latch_main main_29 (.D_in(In[4]), .Clk(main_1_clk_o), .OE(OE), .WE(WE), .D_out(Out[4]));
  D_latch_main main_30 (.D_in(In[2]), .Clk(main_1_clk_o), .OE(OE), .WE(WE), .D_out(Out[2]));
  D_latch_main main_31 (.D_in(In[3]), .Clk(main_1_clk_o), .OE(OE), .WE(WE), .D_out(Out[3]));
  D_latch_main main_32 (.D_in(In[0]), .Clk(main_1_clk_o), .OE(OE), .WE(WE), .D_out(Out[0]));
  D_latch_main main_33 (.D_in(In[1]), .Clk(main_1_clk_o), .OE(OE), .WE(WE), .D_out(Out[1]));
endmodule
