// Logisim project 4-16 Decoder.circ as structural Verilog: 1 circuit, main circuit main
module main (
  input  [3:0] In,
  output [15:0] Out
);

  wire not_1_out;
  wire [7:0] main_1_out_4, main_2_out_4;

  Pull_Resistor pull_resistor_1 (.node(Out[7:0]));
  not not_1 (not_1_out, In[3]);
  Pull_Resistor pull_resistor_2 (.node(Out[15:8]));
  assign Out[7:0] = not_1_out ? main_1_out_4 : 8'bz;  // Controlled_Buffer controlled_buffer_1
  assign Out[15:8] = In[3] ? main_2_out_4 : 8'bz;  // Controlled_Buffer controlled_buffer_2
  _3_8_decoder_main main_1 (
    .out_4(main_1_out_4[0]), .out_5(main_1_out_4[1]), .out_6(main_1_out_4[2]), .out_7(main_1_out_4[3]),
    .out_8(main_1_out_4[4]), .out_9(main_1_out_4[5]), .out_10(main_1_out_4[6]), .out_11(main_1_out_4[7]),
    .in_1(In[0]), .in_2(In[1]), .in_3(In[2]));
  _3_8_decoder_main main_2 (
    .out_4(main_2_out_4[0]), .out_5(main_2_out_4[1]), .out_6(main_2_out_4[2]), .out_7(main_2_out_4[3]),
    .out_8(main_2_out_4[4]), .out_9(main_2_out_4[5]), .out_10(main_2_out_4[6]), .out_11(main_2_out_4[7]),
    .in_1(In[0]), .in_2(In[1]), .in_3(In[2]));
endmodule
