// Logisim project 8_bit_D_register.circ as structural Verilog: 1 circuit, main circuit main
module main (
  input  Clk,
  input  OE,
  input  WE,
  input  [7:0] In,
  output [7:0] Out
);

  wire main_1_clk_o;

  Rising_edge_main main_1 (.CLK_i(Clk), .CLK_o(main_1_clk_o));
  D_latch_main main_2 (.D_in(In[6]), .Clk(main_1_clk_o), .OE(OE), .WE(WE), .D_out(Out[6]));
  D_latch_main main_3 (.D_in(In[7]), .Clk(main_1_clk_o), .OE(OE), .WE(WE), .D_out(Out[7]));
  D_latch_main main_4 (.D_in(In[5]), .Clk(main_1_clk_o), .OE(OE), .WE(WE), .D_out(Out[5]));
  D_latch_main main_5 (.D_in(In[3]), .Clk(main_1_clk_o), .OE(OE), .WE(WE), .D_out(Out[3]));
  D_latch_main main_6 (.D_in(In[4]), .Clk(main_1_clk_o), .OE(OE), .WE(WE), .D_out(Out[4]));
  D_latch_main main_7 (.D_in(In[2]), .Clk(main_1_clk_o), .OE(OE), .WE(WE), .D_out(Out[2]));
  D_latch_main main_8 (.D_in(In[0]), .Clk(main_1_clk_o), .OE(OE), .WE(WE), .D_out(Out[0]));
  D_latch_main main_9 (.D_in(In[1]), .Clk(main_1_clk_o), .OE(OE), .WE(WE), .D_out(Out[1]));
endmodule
