// Logisim project ALU.circ as structural Verilog: 1 circuit, main circuit main
module main (
  input  [15:0] A_BUS,
  input  [15:0] B_BUS,
  input  [3:0] INS,
  output ZERO,
  output [15:0] C_BUS
);

  wire nand_1_out, not_1_out, not_2_out, not_3_out, not_4_out, pull_resistor_3_node;
  wire [15:0] main_5_s0, pull_resistor_1_node, pull_resistor_2_node;

  Pull_Resistor pull_resistor_1 (.node(pull_resistor_1_node));
  _16_bit_tristate_buffer_main main_1 (
    .In(pull_resistor_1_node), .Out(C_BUS), .S0(not_1_out), .S1(INS[1]), .S2(INS[2]), .S3(not_4_out));
  _16_bit_tristate_buffer_main main_2 (
    .In(B_BUS), .Out(C_BUS), .S0(INS[0]), .S1(not_2_out), .S2(INS[2]), .S3(not_4_out));
  _16_bit_tristate_buffer_main main_3 (
    .In(A_BUS), .Out(C_BUS), .S0(not_1_out), .S1(not_2_out), .S2(INS[2]), .S3(not_4_out));
  _16_bit_tristate_buffer_main main_4 (
    .In(main_5_s0), .Out(C_BUS), .S0(1'b1), .S1(1'b1), .S2(not_3_out), .S3(not_4_out));
  Pull_Resistor pull_resistor_2 (.node(pull_resistor_2_node));
  assign pull_resistor_2_node = nand_1_out ? B_BUS : 16'bz;  // Controlled_Buffer controlled_buffer_1
  nand nand_1 (nand_1_out, INS[0], INS[1]);
  _16_BIT_ADD_SUB_main main_5 (
    .B15(A_BUS[15]), .B14(A_BUS[14]), .B13(A_BUS[13]), .B12(A_BUS[12]), .B11(A_BUS[11]), .B10(A_BUS[10]),
    .B9(A_BUS[9]), .B8(A_BUS[8]), .B7(A_BUS[7]), .B6(A_BUS[6]), .B5(A_BUS[5]), .B4(A_BUS[4]), .B3(A_BUS[3]),
    .B2(A_BUS[2]), .B1(A_BUS[1]), .B0(A_BUS[0]), .A15(pull_resistor_2_node[15]),
    .A14(pull_resistor_2_node[14]), .A13(pull_resistor_2_node[13]), .A12(pull_resistor_2_node[12]),
    .A11(pull_resistor_2_node[11]), .A10(pull_resistor_2_node[10]), .A9(pull_resistor_2_node[9]),
    .A8(pull_resistor_2_node[8]), .A7(pull_resistor_2_node[7]), .A6(pull_resistor_2_node[6]),
    .A5(pull_resistor_2_node[5]), .A4(pull_resistor_2_node[4]), .A3(pull_resistor_2_node[3]),
    .A2(pull_resistor_2_node[2]), .A1(pull_resistor_2_node[1]), .A0(pull_resistor_2_node[0]),
    .S15(main_5_s0[15]), .S14(main_5_s0[14]), .S13(main_5_s0[13]), .S12(main_5_s0[12]), .S11(main_5_s0[11]),
    .S10(main_5_s0[10]), .S9(main_5_s0[9]), .S8(main_5_s0[8]), .S7(main_5_s0[7]), .S6(main_5_s0[6]),
    .S5(main_5_s0[5]), .S4(main_5_s0[4]), .S3(main_5_s0[3]), .S2(main_5_s0[2]), .S1(main_5_s0[1]),
    .S0(main_5_s0[0]), .SUB(pull_resistor_3_node), .C_IN(INS[1]));  // open: Overflow
  Pull_Resistor pull_resistor_3 (.node(pull_resistor_3_node));
  and and_1 (pull_resistor_3_node, not_2_out, INS[0]);
  not not_1 (not_1_out, INS[0]);
  not not_2 (not_2_out, INS[1]);
  not not_3 (not_3_out, INS[2]);
  not not_4 (not_4_out, INS[3]);
  nor nor_1 (ZERO, C_BUS[0], C_BUS[1], C_BUS[2], C_BUS[3], C_BUS[4], C_BUS[5], C_BUS[6], C_BUS[7], C_BUS[8], C_BUS[9], C_BUS[10], C_BUS[11], C_BUS[12], C_BUS[13], C_BUS[14], C_BUS[15]);
endmodule
