// Logisim project BUS 2-1 MUX.circ as structural Verilog: 1 circuit, main circuit main
module main (
  input  [15:0] MEM_BUS,
  input  MEM_RD,
  input  [15:0] C_BUS,
  output [15:0] OUTPUT
);

  wire not_1_out;

  not not_1 (not_1_out, MEM_RD);
  assign OUTPUT = not_1_out ? C_BUS : 16'bz;  // Controlled_Buffer controlled_buffer_1
  assign OUTPUT = MEM_RD ? MEM_BUS : 16'bz;  // Controlled_Buffer controlled_buffer_2
endmodule
