// Logisim project BUS_selector.circ as structural Verilog: 1 circuit, main circuit main
module main (
  input  [15:0] D_IN,
  input  A_EN,
  input  B_EN,
  output OE,
  output [15:0] A_BUS,
  output [15:0] B_BUS
);

  or or_1 (OE, B_EN, A_EN);
  assign A_BUS = A_EN ? D_IN : 16'bz;  // Controlled_Buffer controlled_buffer_1
  assign B_BUS = B_EN ? D_IN : 16'bz;  // Controlled_Buffer controlled_buffer_2
endmodule
