// Logisim project CPU.circ as structural Verilog: 1 circuit, main circuit main
module main (
  input  in_1,
  input  [15:0] in_2,
  input  [15:0] in_3,
  input  in_4,
  input  in_5,
  input  MEM_READ,
  input  [3:0] in_7,
  input  MEM_WRITE,
  input  in_9,
  input  [3:0] in_10,
  input  [11:0] in_11,
  input  in_12,
  input  in_13,
  input  [3:0] in_14,
  input  in_15
);

  wire decoder_1_out0, decoder_1_out1, decoder_1_out2, decoder_1_out3, main_1_oe, main_2_oe, main_4_oe,
       main_5_oe, main_6_oe, main_7_oe, main_8_oe, main_9_oe, not_1_out, or_1_out, or_2_out, or_3_out,
       or_4_out, or_5_out, or_6_out, pull_resistor_1_node;
  wire [3:0] controlled_buffer_3_out, controlled_buffer_6_out, controlled_buffer_7_out;
  wire [6:0] MBR_out_2, multiplexer_2_out, rom_1_data;
  wire [8:0] MBR_out;
  wire [15:0] A_SEL_out, B_SEL_out, H1_out, H2_out, H3_out, H4_out, main_1_a_bus, main_1_b_bus,
       main_10_c_bus, MAR_out, MDR_out, MEM_C_SELECT_output, multiplexer_1_out, PC_out, ram_1_data, SP_out,
       TOS_out;
  wire [31:0] controlled_buffer_1_out;

  assign controlled_buffer_1_out[14:3] = in_13 ? in_11 : 12'bz;  // Controlled_Buffer controlled_buffer_1
  Decoder #(.select(2), .disabled(0)) decoder_1 (
    .out0(decoder_1_out0), .out1(decoder_1_out1), .out2(decoder_1_out2), .out3(decoder_1_out3));  // open: sel, en
  RAM #(.addrWidth(16), .dataWidth(16), .bus("separate")) ram_1 (
    .addr(multiplexer_1_out), .din(MDR_out), .data(ram_1_data), .str(MEM_WRITE), .sel(1'b1), .clk(in_1),
    .ld(1'b1), .clr(1'b0));
  or or_1 (or_1_out, MEM_READ, controlled_buffer_1_out[13]);
  BUS_2_1_MUX_main MEM_C_SELECT (
    .MEM_RD(MEM_READ), .C_BUS(main_10_c_bus), .MEM_BUS(ram_1_data), .OUTPUT(MEM_C_SELECT_output));
  or or_2 (or_2_out, controlled_buffer_1_out[6], decoder_1_out0);
  or or_3 (or_3_out, controlled_buffer_1_out[5], decoder_1_out1);
  or or_4 (or_4_out, controlled_buffer_1_out[4], decoder_1_out2);
  or or_5 (or_5_out, controlled_buffer_1_out[3], decoder_1_out3);
  _16_bit_D_register_main MAR (
    .Clk(in_1), .OE(1'b1), .WE(controlled_buffer_1_out[14]), .Out(MAR_out), .In(main_10_c_bus));
  _16_bit_D_register_main MDR (.Clk(in_1), .OE(or_6_out), .WE(or_1_out), .Out(MDR_out), .In(MEM_C_SELECT_output));
  _16_bit_D_register_main PC (
    .Clk(in_1), .OE(1'b1), .WE(controlled_buffer_1_out[12]), .Out(PC_out), .In(main_10_c_bus));
  _16_bit_D_register_main MBR (.Clk(in_1), .OE(1'b1), .WE(1'b1), .Out({MBR_out_2, MBR_out}), .In(ram_1_data));
  _16_bit_D_register_main SP (
    .Clk(in_1), .OE(main_4_oe), .WE(controlled_buffer_1_out[11]), .Out(SP_out), .In(main_10_c_bus));
  _16_bit_D_register_main TOS (
    .Clk(in_1), .OE(main_5_oe), .WE(controlled_buffer_1_out[10]), .Out(TOS_out), .In(main_10_c_bus));
  _16_bit_D_register_main H1 (.Clk(in_1), .OE(main_6_oe), .WE(or_2_out), .Out(H1_out), .In(main_10_c_bus));
  _16_bit_D_register_main H2 (.Clk(in_1), .OE(main_7_oe), .WE(or_3_out), .Out(H2_out), .In(main_10_c_bus));
  _16_bit_D_register_main H3 (.Clk(in_1), .OE(main_8_oe), .WE(or_4_out), .Out(H3_out), .In(main_10_c_bus));
  _16_bit_D_register_main H4 (.Clk(in_1), .OE(main_9_oe), .WE(or_5_out), .Out(H4_out), .In(main_10_c_bus));
  Multiplexer #(.width(16), .enable("false")) multiplexer_1 (
    .in0(MAR_out), .in1(PC_out), .out(multiplexer_1_out), .sel(pull_resistor_1_node));
  or or_6 (or_6_out, MEM_WRITE, main_1_oe);
  BUS_selector_main main_1 (
    .OE(main_1_oe), .D_IN(MDR_out), .A_EN(A_SEL_out[1]), .B_EN(B_SEL_out[1]), .A_BUS(main_1_a_bus),
    .B_BUS(main_1_b_bus));
  BUS_selector_main main_2 (
    .OE(main_2_oe), .D_IN(PC_out), .A_EN(A_SEL_out[2]), .B_EN(B_SEL_out[2]), .A_BUS(main_1_a_bus),
    .B_BUS(main_1_b_bus));
  BUS_selector_main main_3 (
    .D_IN({MBR_out_2, MBR_out}), .A_EN(A_SEL_out[3]), .B_EN(B_SEL_out[3]), .A_BUS(main_1_a_bus),
    .B_BUS(main_1_b_bus));  // open: OE
  BUS_selector_main main_4 (
    .OE(main_4_oe), .D_IN(SP_out), .A_EN(A_SEL_out[4]), .B_EN(B_SEL_out[4]), .A_BUS(main_1_a_bus),
    .B_BUS(main_1_b_bus));
  BUS_selector_main main_5 (
    .OE(main_5_oe), .D_IN(TOS_out), .A_EN(A_SEL_out[5]), .B_EN(B_SEL_out[5]), .A_BUS(main_1_a_bus),
    .B_BUS(main_1_b_bus));
  BUS_selector_main main_6 (
    .OE(main_6_oe), .D_IN(H1_out), .A_EN(A_SEL_out[12]), .B_EN(B_SEL_out[12]), .A_BUS(main_1_a_bus),
    .B_BUS(main_1_b_bus));
  BUS_selector_main main_7 (
    .OE(main_7_oe), .D_IN(H2_out), .A_EN(A_SEL_out[13]), .B_EN(B_SEL_out[13]), .A_BUS(main_1_a_bus),
    .B_BUS(main_1_b_bus));
  BUS_selector_main main_8 (
    .OE(main_8_oe), .D_IN(H3_out), .A_EN(A_SEL_out[14]), .B_EN(B_SEL_out[14]), .A_BUS(main_1_a_bus),
    .B_BUS(main_1_b_bus));
  BUS_selector_main main_9 (
    .OE(main_9_oe), .D_IN(H4_out), .A_EN(A_SEL_out[15]), .B_EN(B_SEL_out[15]), .A_BUS(main_1_a_bus),
    .B_BUS(main_1_b_bus));
  Pull_Resistor #(.pull(1)) pull_resistor_1 (.node(pull_resistor_1_node));
  assign main_1_b_bus = in_4 ? in_2 : 16'bz;  // Controlled_Buffer controlled_buffer_2
  // OR_Gate OE_SIG_FOR_PC has open pins: in0=pull_resistor_1_node, in1=main_2_oe, out=open
  assign controlled_buffer_3_out = in_15 ? in_14 : 4'bz;  // Controlled_Buffer controlled_buffer_3
  ALU_main main_10 (.A_BUS(main_1_a_bus), .B_BUS(main_1_b_bus), .C_BUS(main_10_c_bus), .INS(controlled_buffer_3_out));
  assign controlled_buffer_3_out = not_1_out ? controlled_buffer_1_out[20:17] : 4'bz;  // Controlled_Buffer controlled_buffer_4
  not not_1 (not_1_out, in_15);
  assign main_1_a_bus = in_5 ? in_3 : 16'bz;  // Controlled_Buffer controlled_buffer_5
  _4_16_Decoder_main A_SEL (.Out(A_SEL_out), .In(controlled_buffer_6_out));
  _4_16_Decoder_main B_SEL (.Out(B_SEL_out), .In(controlled_buffer_7_out));
  assign controlled_buffer_6_out = in_9 ? in_7 : 4'bz;  // Controlled_Buffer controlled_buffer_6
  assign controlled_buffer_7_out = in_12 ? in_10 : 4'bz;  // Controlled_Buffer controlled_buffer_7
  Multiplexer #(.width(7), .enable("false")) multiplexer_2 (
    .in0(rom_1_data), .in1(MBR_out_2), .out(multiplexer_2_out), .sel(pull_resistor_1_node));
  // NOR_Gate nor_1 has open pins: in0=MBR_out[8], in1=MBR_out[7], in2=MBR_out[6], out=open
  ROM #(.dataWidth(32)) rom_1 (
    .addr({1'b0, multiplexer_2_out}),
    .data({controlled_buffer_1_out[31], rom_1_data, controlled_buffer_1_out[23:3], MEM_WRITE, MEM_READ, controlled_buffer_1_out[0]}),
    .sel(1'b1));
  ROM rom_2 (.addr({1'b0, multiplexer_2_out}), .data({controlled_buffer_6_out, controlled_buffer_7_out}), .sel(1'b1));

  // Notes on the sheet:
  //   contents of rom_1 (hex, n*v repeats v):
  //   4*800000 5064002
  //   contents of rom_2 (hex, n*v repeats v):
  //   4*0 20
endmodule
