// Logisim project CPU_V2.circ as structural Verilog: 1 circuit, main circuit main
module main (
  input  in_1,
  input  MEM_WRITE,
  input  MEM_READ,
  input  in_4,
  input  PC_RESET,
  input  [11:0] in_6,
  input  in_7,
  input  [3:0] in_8,
  input  in_9,
  output [15:0] out_10,
  output [15:0] TIME_STAMP
);

  wire and_1_out, and_2_out, CLK, clock_2_out, counter_1_carry, decoder_1_out1, decoder_1_out2,
       decoder_1_out3, decoder_1_out4, decoder_1_out5, decoder_1_out6, decoder_1_out7, decoder_1_out12,
       decoder_1_out13, decoder_1_out14, decoder_1_out15, decoder_2_out1, decoder_2_out2, decoder_2_out3,
       decoder_2_out4, decoder_2_out5, decoder_2_out6, decoder_2_out7, decoder_2_out12, decoder_2_out13,
       decoder_2_out14, decoder_2_out15, F_NMS, F_ZERO, H_BIT, JMPC, JNMS, JZERO, main_5_oe, main_6_oe,
       main_7_oe, main_9_oe, main_10_oe, main_11_oe, multiplexer_1_out, multiplexer_2_out, or_1_out, R, W;
  wire [3:0] ALU, multiplexer_6_out, multiplexer_7_out, multiplexer_8_out, register_2_q, register_2_q_2;
  wire [7:0] multiplexer_9_out, rom_2_data, ROM_ADDR;
  wire [11:0] C_BUS_SELECT, multiplexer_3_out;
  wire [15:0] H1_out, H2_out, H3_out, LV_out, main_1_a_bus, main_1_b_bus, MAR_out, MBR_DATA, MEM_ADDR,
       MEM_D_IN, MEM_D_OUT, multiplexer_4_out, PC_p1, PC_p6, SADD, TOS_out;
  wire [16:0] register_1_q;
  wire [31:0] rom_1_data;

  Multiplexer #(.disabled(0), .enable("false")) multiplexer_1 (
    .in0(W), .in1(MEM_WRITE), .out(multiplexer_1_out), .sel(in_1));
  Multiplexer #(.disabled(0), .enable("false")) multiplexer_2 (
    .in0(R), .in1(MEM_READ), .out(multiplexer_2_out), .sel(in_1));
  RAM #(.addrWidth(16), .dataWidth(16), .bus("separate")) ram_1 (
    .addr(MEM_ADDR), .din(MEM_D_IN), .data(MEM_D_OUT), .str(multiplexer_1_out), .sel(1'b1), .clk(CLK),
    .ld(1'b1), .clr(1'b0));
  Multiplexer #(.width(12), .disabled(0), .enable("false")) multiplexer_3 (
    .in0(C_BUS_SELECT), .in1(in_6), .out(multiplexer_3_out), .sel(in_7));
  or or_1 (or_1_out, multiplexer_2_out, multiplexer_3_out[10]);
  Multiplexer #(.width(16), .enable("false")) multiplexer_4 (
    .in0(PC_p1), .in1(MEM_D_OUT), .out(multiplexer_4_out), .sel(multiplexer_2_out));
  Clock clock_1 (.out(CLK));
  _16_bit_D_register_main MAR (.Clk(CLK), .OE(1'b1), .WE(multiplexer_3_out[11]), .Out(MAR_out), .In(PC_p1));
  _16_bit_D_register_main MDR (.Clk(CLK), .OE(1'b1), .WE(or_1_out), .Out(MEM_D_IN), .In(multiplexer_4_out));
  // PC_module_main PC: pin names not known; wires that end beside it: PC_p1, multiplexer_3_out[9], JMPC, PC_RESET, CLK, PC_p6
  _16_bit_D_register_main MBR (.Clk(CLK), .OE(1'b1), .WE(JMPC), .Out(MBR_DATA), .In(MEM_D_OUT));
  _16_bit_D_register_main u_SADD (.Clk(CLK), .OE(main_5_oe), .WE(multiplexer_3_out[8]), .Out(SADD), .In(PC_p1));
  _16_bit_D_register_main LV (.Clk(CLK), .OE(main_6_oe), .WE(multiplexer_3_out[7]), .Out(LV_out), .In(PC_p1));
  _16_bit_D_register_main TOS (.Clk(CLK), .OE(main_7_oe), .WE(multiplexer_3_out[6]), .Out(TOS_out), .In(PC_p1));
  _16_bit_D_register_main H0 (.Clk(CLK), .OE(1'b1), .WE(multiplexer_3_out[3]), .Out(out_10), .In(PC_p1));
  _16_bit_D_register_main H1 (.Clk(CLK), .OE(main_9_oe), .WE(multiplexer_3_out[2]), .Out(H1_out), .In(PC_p1));
  _16_bit_D_register_main H2 (.Clk(CLK), .OE(main_10_oe), .WE(multiplexer_3_out[1]), .Out(H2_out), .In(PC_p1));
  _16_bit_D_register_main H3 (.Clk(CLK), .OE(main_11_oe), .WE(multiplexer_3_out[0]), .Out(H3_out), .In(PC_p1));
  Multiplexer #(.width(16), .enable("false")) multiplexer_5 (
    .in0(PC_p6), .in1(MAR_out), .out(MEM_ADDR), .sel(multiplexer_1_out));
  BUS_selector_main main_1 (
    .D_IN(MAR_out), .A_EN(decoder_1_out1), .B_EN(decoder_2_out1), .A_BUS(main_1_a_bus), .B_BUS(main_1_b_bus));  // open: OE
  BUS_selector_main main_2 (
    .D_IN(MEM_D_IN), .A_EN(decoder_1_out2), .B_EN(decoder_2_out2), .A_BUS(main_1_a_bus), .B_BUS(main_1_b_bus));  // open: OE
  BUS_selector_main main_3 (
    .D_IN(PC_p6), .A_EN(decoder_1_out3), .B_EN(decoder_2_out3), .A_BUS(main_1_a_bus), .B_BUS(main_1_b_bus));  // open: OE
  BUS_selector_main main_4 (
    .D_IN(MBR_DATA), .A_EN(decoder_1_out4), .B_EN(decoder_2_out4), .A_BUS(main_1_a_bus), .B_BUS(main_1_b_bus));  // open: OE
  BUS_selector_main main_5 (
    .OE(main_5_oe), .D_IN(SADD), .A_EN(decoder_1_out5), .B_EN(decoder_2_out5), .A_BUS(main_1_a_bus),
    .B_BUS(main_1_b_bus));
  BUS_selector_main main_6 (
    .OE(main_6_oe), .D_IN(LV_out), .A_EN(decoder_1_out6), .B_EN(decoder_2_out6), .A_BUS(main_1_a_bus),
    .B_BUS(main_1_b_bus));
  BUS_selector_main main_7 (
    .OE(main_7_oe), .D_IN(TOS_out), .A_EN(decoder_1_out7), .B_EN(decoder_2_out7), .A_BUS(main_1_a_bus),
    .B_BUS(main_1_b_bus));
  BUS_selector_main main_8 (
    .D_IN(out_10), .A_EN(decoder_1_out12), .B_EN(decoder_2_out12), .A_BUS(main_1_a_bus), .B_BUS(main_1_b_bus));  // open: OE
  BUS_selector_main main_9 (
    .OE(main_9_oe), .D_IN(H1_out), .A_EN(decoder_1_out13), .B_EN(decoder_2_out13), .A_BUS(main_1_a_bus),
    .B_BUS(main_1_b_bus));
  BUS_selector_main main_10 (
    .OE(main_10_oe), .D_IN(H2_out), .A_EN(decoder_1_out14), .B_EN(decoder_2_out14), .A_BUS(main_1_a_bus),
    .B_BUS(main_1_b_bus));
  BUS_selector_main main_11 (
    .OE(main_11_oe), .D_IN(H3_out), .A_EN(decoder_1_out15), .B_EN(decoder_2_out15), .A_BUS(main_1_a_bus),
    .B_BUS(main_1_b_bus));
  ALU_main main_12 (.A_BUS(main_1_a_bus), .B_BUS(main_1_b_bus), .ZERO(F_ZERO), .C_BUS(PC_p1), .INS(multiplexer_6_out));
  Multiplexer #(.width(4), .enable("false")) multiplexer_6 (.in0(ALU), .in1(in_8), .out(multiplexer_6_out), .sel(in_9));
  Decoder #(.select(4), .disabled(0), .enable("false")) decoder_1 (
    .out1(decoder_1_out1), .out2(decoder_1_out2), .out3(decoder_1_out3), .out4(decoder_1_out4),
    .out5(decoder_1_out5), .out6(decoder_1_out6), .out7(decoder_1_out7), .out12(decoder_1_out12),
    .out13(decoder_1_out13), .out14(decoder_1_out14), .out15(decoder_1_out15), .sel(multiplexer_7_out));  // open: out0, out8, out9, out10, out11
  Decoder #(.select(4), .disabled(0), .enable("false")) decoder_2 (
    .out1(decoder_2_out1), .out2(decoder_2_out2), .out3(decoder_2_out3), .out4(decoder_2_out4),
    .out5(decoder_2_out5), .out6(decoder_2_out6), .out7(decoder_2_out7), .out12(decoder_2_out12),
    .out13(decoder_2_out13), .out14(decoder_2_out14), .out15(decoder_2_out15), .sel(multiplexer_8_out));  // open: out0, out8, out9, out10, out11
  Multiplexer #(.width(4), .disabled(0), .enable("false")) multiplexer_7 (
    .in0(register_2_q_2), .in1(MBR_DATA[3:0]), .out(multiplexer_7_out), .sel(register_1_q[16]));
  Multiplexer #(.width(4), .disabled(0), .enable("false")) multiplexer_8 (
    .in0(register_2_q), .in1(MBR_DATA[3:0]), .out(multiplexer_8_out), .sel(register_1_q[15]));
  and and_1 (and_1_out, F_ZERO, JZERO);
  and and_2 (and_2_out, F_NMS, JNMS);
  or or_2 (H_BIT, and_1_out, and_2_out);
  Multiplexer #(.width(8), .disabled(0), .enable("false")) multiplexer_9 (
    .in0(ROM_ADDR), .in1({in_4, MBR_DATA[15:9]}), .out(multiplexer_9_out), .sel(JMPC));
  Clock clock_2 (.out(clock_2_out));
  Counter #(.width(19), .max('h7ffff)) counter_1 (
    .load(1'b0), .count(1'b1), .carry(counter_1_carry), .clk(clock_2_out), .clr(1'b0));  // open: D, Q
  ROM #(.addrWidth(9), .dataWidth(32)) rom_1 (.addr({H_BIT, multiplexer_9_out}), .data(rom_1_data), .sel(1'b1));
  Register #(.width(32)) register_1 (
    .D(rom_1_data), .en(1'b1),
    .Q({ROM_ADDR, JMPC, JZERO, JNMS, ALU, register_1_q[16:15], C_BUS_SELECT, W, R, register_1_q[0]}),
    .clk(CLK), .clr(1'b0));
  nor nor_1 (F_NMS, SADD[0], SADD[1], SADD[2]);
  Counter #(.width(16), .max('hffff)) counter_2 (
    .load(1'b0), .count(1'b1), .Q(TIME_STAMP), .clk(counter_1_carry), .clr(1'b0));  // open: D, carry
  ROM #(.addrWidth(9)) rom_2 (.addr({H_BIT, multiplexer_9_out}), .data(rom_2_data), .sel(1'b1));
  Register register_2 (.D(rom_2_data), .en(1'b1), .Q({register_2_q_2, register_2_q}), .clk(CLK), .clr(1'b0));

  // Notes on the sheet:
  //   RAM
  //   REGISTER WRITE SIGNAL DECODER
  //   C BUS
  //   BUS SELECTOR ARRAY
  //   B BUS
  //   A BUS
  //   ALU
  //   A BUS SELECT DECODER
  //   B BUS SELECT DECODER
  //   HIGH BIT LOGIC CIRCUIT
  //   A REG CONTROL SIGNAL
  //   B REG CONTROL SIGNAL
  //   MBR REGISTER SELECT UTILIY
  //   PRESCALER
  //   MICRO INSTRUCTION MEMORY
  //   contents of rom_1 (hex, n*v repeats v):
  //   4*800000 5084002 6880078
  //   TIME STAMP CIRCUIT
  //   COUNTING REG
  //   8 SENSOR FLAG CIRCUIT
  //   contents of rom_2 (hex, n*v repeats v):
  //   4*0 30 20
endmodule
