// Logisim project D_latch.circ as structural Verilog: 1 circuit, main circuit main
module main (
  input  D_in,
  input  Clk,
  input  OE,
  input  WE,
  output D_out
);

  wire controlled_buffer_1_out, nand_1_out, nand_2_out, nand_3_out, nand_4_out, not_1_out;

  assign controlled_buffer_1_out = WE ? Clk : 1'bz;  // Controlled_Buffer controlled_buffer_1
  Pull_Resistor pull_resistor_1 (.node(controlled_buffer_1_out));
  not not_1 (not_1_out, D_in);
  nand nand_1 (nand_1_out, D_in, controlled_buffer_1_out);
  nand nand_2 (nand_2_out, controlled_buffer_1_out, not_1_out);
  nand nand_3 (nand_3_out, nand_1_out, nand_4_out);
  nand nand_4 (nand_4_out, nand_3_out, nand_2_out);
  assign D_out = OE ? nand_3_out : 1'bz;  // Controlled_Buffer controlled_buffer_2
endmodule
