// Logisim project PC_module.circ as structural Verilog: 1 circuit, main circuit main
module main (
  input  CLK,
  input  COUNT,
  input  WE,
  input  [15:0] D_IN,
  output [15:0] D_OUT
);

  Counter #(.width(16), .max('hffff)) counter_1 (
    .load(WE), .D(D_IN), .count(COUNT), .Q(D_OUT), .clk(CLK), .clr(1'b0));  // open: carry
endmodule
