// Logisim project Rising_edge.circ as structural Verilog: 1 circuit, main circuit main
module main (
  input  CLK_i,
  output CLK_o
);

  wire not_1_out, not_2_out, not_3_out, not_4_out, not_5_out;

  not not_1 (not_1_out, CLK_i);
  not not_2 (not_2_out, not_1_out);
  not not_3 (not_3_out, not_2_out);
  not not_4 (not_4_out, not_5_out);
  not not_5 (not_5_out, not_3_out);
  and and_1 (CLK_o, not_4_out, CLK_i);
endmodule
