// Logisim project exp.circ as structural Verilog: 1 circuit, main circuit main
module main (
  input  [7:0] in_1,
  input  in_2,
  output [31:0] out_3
);

  ROM #(.dataWidth(32)) rom_1 (.addr(in_1), .data(out_3), .sel(in_2));

  // Notes on the sheet:
  //   contents of rom_1 (hex, n*v repeats v):
  //   7382 15*0 dfd 30*0 31f4
endmodule
